// Digital circuit Exo1_et_2.dig as structural Verilog
module Exo1_et_2 (
  input  clk,
  input  in_2,
  input  in_3,
  input  in_4
);

  wire d_ff_1_q, d_ff_2_q, d_ff_3_q, d_ff_4_q, d_ff_5_q, d_ff_6_q, d_ff_7_q, d_ff_8_q, d_ff_9_q, d_ff_10_nq,
       lookuptable_1_out, lookuptable_2_out, lookuptable_3_out, lookuptable_4_out, lookuptable_5_out,
       lookuptable_6_out, lookuptable_7_out, lookuptable_8_out, lookuptable_9_out, lookuptable_10_out,
       lookuptable_11_out, lookuptable_12_out, lookuptable_13_out, lookuptable_14_out, multiplexer_1_out,
       multiplexer_2_out, multiplexer_3_out, multiplexer_4_out, multiplexer_5_out, multiplexer_6_out,
       multiplexer_7_out;

  LED led_1 (.in(d_ff_10_nq));
  LED led_2 (.in(d_ff_1_q));
  LED led_3 (.in(d_ff_2_q));
  D_FF d_ff_1 (.D(d_ff_10_nq), .C(clk), .Q(d_ff_1_q));  // open: nQ
  LED led_4 (.in(d_ff_3_q));
  LED led_5 (.in(d_ff_4_q));
  D_FF d_ff_2 (.D(d_ff_1_q), .C(clk), .Q(d_ff_2_q));  // open: nQ
  LED led_6 (.in(d_ff_5_q));
  LED led_7 (.in(d_ff_6_q));
  D_FF d_ff_3 (.D(d_ff_2_q), .C(clk), .Q(d_ff_3_q));  // open: nQ
  LED led_8 (.in(d_ff_7_q));
  LED led_9 (.in(d_ff_8_q));
  LED led_10 (.in(d_ff_9_q));
  D_FF d_ff_4 (.D(d_ff_3_q), .C(clk), .Q(d_ff_4_q));  // open: nQ
  D_FF d_ff_5 (.D(d_ff_4_q), .C(clk), .Q(d_ff_5_q));  // open: nQ
  D_FF d_ff_6 (.D(d_ff_5_q), .C(clk), .Q(d_ff_6_q));  // open: nQ
  D_FF d_ff_7 (.D(d_ff_6_q), .C(clk), .Q(d_ff_7_q));  // open: nQ
  D_FF d_ff_8 (.D(d_ff_7_q), .C(clk), .Q(d_ff_8_q));  // open: nQ
  D_FF d_ff_9 (.D(d_ff_8_q), .C(clk), .Q(d_ff_9_q));  // open: nQ
  D_FF d_ff_10 (.D(d_ff_9_q), .C(clk), .nQ(d_ff_10_nq));  // open: Q
  LookUpTable lookuptable_1 (
    .in0(d_ff_10_nq), .in1(d_ff_1_q), .in2(d_ff_2_q), .in3(d_ff_3_q), .in4(d_ff_4_q), .in5(d_ff_5_q),
    .out(lookuptable_1_out));
  LookUpTable lookuptable_2 (
    .in0(d_ff_10_nq), .in1(d_ff_1_q), .in2(d_ff_2_q), .in3(d_ff_3_q), .in4(d_ff_4_q), .in5(d_ff_5_q),
    .out(lookuptable_2_out));
  LookUpTable lookuptable_3 (
    .in0(d_ff_10_nq), .in1(d_ff_1_q), .in2(d_ff_2_q), .in3(d_ff_3_q), .in4(d_ff_4_q), .in5(d_ff_5_q),
    .out(lookuptable_3_out));
  LookUpTable lookuptable_4 (
    .in0(d_ff_10_nq), .in1(d_ff_1_q), .in2(d_ff_2_q), .in3(d_ff_3_q), .in4(d_ff_4_q), .in5(d_ff_5_q),
    .out(lookuptable_4_out));
  LookUpTable lookuptable_5 (
    .in0(d_ff_10_nq), .in1(d_ff_1_q), .in2(d_ff_2_q), .in3(d_ff_3_q), .in4(d_ff_4_q), .in5(d_ff_5_q),
    .out(lookuptable_5_out));
  LookUpTable lookuptable_6 (
    .in0(d_ff_10_nq), .in1(d_ff_1_q), .in2(d_ff_2_q), .in3(d_ff_3_q), .in4(d_ff_4_q), .in5(d_ff_5_q),
    .out(lookuptable_6_out));
  LookUpTable lookuptable_7 (
    .in0(d_ff_10_nq), .in1(d_ff_1_q), .in2(d_ff_2_q), .in3(d_ff_3_q), .in4(d_ff_4_q), .in5(d_ff_5_q),
    .out(lookuptable_7_out));
  LookUpTable lookuptable_8 (
    .in0(d_ff_6_q), .in1(d_ff_7_q), .in2(d_ff_8_q), .in3(d_ff_9_q), .in4(in_3), .in5(in_2),
    .out(lookuptable_8_out));
  LookUpTable lookuptable_9 (
    .in0(d_ff_6_q), .in1(d_ff_7_q), .in2(d_ff_8_q), .in3(d_ff_9_q), .in4(in_3), .in5(in_2),
    .out(lookuptable_9_out));
  Multiplexer multiplexer_1 (
    .sel(d_ff_6_q), .in_0(lookuptable_7_out), .in_1(lookuptable_8_out), .out(multiplexer_1_out));
  Multiplexer multiplexer_2 (
    .sel(d_ff_6_q), .in_0(lookuptable_6_out), .in_1(lookuptable_9_out), .out(multiplexer_2_out));
  LookUpTable lookuptable_10 (
    .in0(d_ff_6_q), .in1(d_ff_7_q), .in2(d_ff_8_q), .in3(d_ff_9_q), .in4(in_3), .in5(in_2),
    .out(lookuptable_10_out));
  Multiplexer multiplexer_3 (
    .sel(d_ff_6_q), .in_0(lookuptable_4_out), .in_1(lookuptable_11_out), .out(multiplexer_3_out));
  Multiplexer multiplexer_4 (
    .sel(d_ff_6_q), .in_0(lookuptable_5_out), .in_1(lookuptable_10_out), .out(multiplexer_4_out));
  Multiplexer multiplexer_5 (
    .sel(d_ff_6_q), .in_0(lookuptable_3_out), .in_1(lookuptable_12_out), .out(multiplexer_5_out));
  LookUpTable lookuptable_11 (
    .in0(d_ff_6_q), .in1(d_ff_7_q), .in2(d_ff_8_q), .in3(d_ff_9_q), .in4(in_3), .in5(in_2),
    .out(lookuptable_11_out));
  Multiplexer multiplexer_6 (
    .sel(d_ff_6_q), .in_0(lookuptable_2_out), .in_1(lookuptable_13_out), .out(multiplexer_6_out));
  Multiplexer multiplexer_7 (
    .sel(d_ff_6_q), .in_0(lookuptable_1_out), .in_1(lookuptable_14_out), .out(multiplexer_7_out));
  LookUpTable lookuptable_12 (
    .in0(d_ff_6_q), .in1(d_ff_7_q), .in2(d_ff_8_q), .in3(d_ff_9_q), .in4(in_3), .in5(in_2),
    .out(lookuptable_12_out));
  Seven_Seg seven_seg_1 (
    .a(multiplexer_7_out), .b(multiplexer_6_out), .c(multiplexer_1_out), .d(multiplexer_2_out),
    .e(multiplexer_5_out), .f(multiplexer_3_out), .g(multiplexer_4_out), .dp(in_4));
  LookUpTable lookuptable_13 (
    .in0(d_ff_6_q), .in1(d_ff_7_q), .in2(d_ff_8_q), .in3(d_ff_9_q), .in4(in_3), .in5(in_2),
    .out(lookuptable_13_out));
  LookUpTable lookuptable_14 (
    .in0(d_ff_6_q), .in1(d_ff_7_q), .in2(d_ff_8_q), .in3(d_ff_9_q), .in4(in_3), .in5(in_2),
    .out(lookuptable_14_out));

  // Notes on the sheet:
  //   contents of lookuptable_1 (hex, n*v repeats v):
  //   31*0,1,31*0,1
  //   contents of lookuptable_2 (hex, n*v repeats v):
  //   0,1,29*0,1,31*0,1
  //   contents of lookuptable_3 (hex, n*v repeats v):
  //   0,1,5*0,1
  //   contents of lookuptable_4 (hex, n*v repeats v):
  //   0,1,5*0,1,7*0,1,47*0,1
  //   contents of lookuptable_5 (hex, n*v repeats v):
  //   0,1,0,1,11*0,1,15*0,1,31*0,1
  //   contents of lookuptable_6 (hex, n*v repeats v):
  //   0,1,0,1,0,0,0,1,7*0,1,15*0,1
  //   contents of lookuptable_7 (hex, n*v repeats v):
  //   0,1,5*0,1,7*0,1,47*0,1
  //   contents of lookuptable_8 (hex, n*v repeats v):
  //   0,1,0,1,0,0,0,1,7*0,1
  //   contents of lookuptable_9 (hex, n*v repeats v):
  //   0,0,0,1,0,0,0,1,7*0,1
  //   contents of lookuptable_10 (hex, n*v repeats v):
  //   0,1,0,1,0,0,0,1,7*0,1
  //   contents of lookuptable_11 (hex, n*v repeats v):
  //   0,1,5*0,1,7*0,1
  //   contents of lookuptable_12 (hex, n*v repeats v):
  //   0,1,5*0,1
  //   contents of lookuptable_13 (hex, n*v repeats v):
  //   0,1,5*0,1,7*0,1
  //   contents of lookuptable_14 (hex, n*v repeats v):
  //   0,1,5*0,1,7*0,1
endmodule
