// Digital circuit exo3_4.dig as structural Verilog
module exo3_4 (
  input  clk,
  output out_2,
  output out_3,
  output out_4
);

  wire d_ff_4_nq;

  D_FF d_ff_1 (.D(d_ff_4_nq), .C(clk), .Q(out_2));  // open: nQ
  D_FF d_ff_2 (.D(out_2), .C(clk), .Q(out_3));  // open: nQ
  D_FF d_ff_3 (.D(out_3), .C(clk), .Q(out_4));  // open: nQ
  D_FF d_ff_4 (.D(out_4), .C(clk), .nQ(d_ff_4_nq));  // open: Q
endmodule
